# Fritzing sketch nRF24L01-RPi (saved by Fritzing 0.9.0b)

parts:
  Raspberry_Pi_B_rev1 = Raspberry Pi B rev2
  NRF24L1 = NRF24L01

nets:
  3V3: Raspberry_Pi_B_rev1.3V3, NRF24L1.VCC
  N1: Raspberry_Pi_B_rev1.GPIO_24, NRF24L1.IRQ
  N2: Raspberry_Pi_B_rev1.GPIO_10, NRF24L1.MOSI
  N3: Raspberry_Pi_B_rev1.GPIO_9, NRF24L1.MISO
  N4: Raspberry_Pi_B_rev1.GPIO_25, NRF24L1.CE
  N5: Raspberry_Pi_B_rev1.GPIO_11, NRF24L1.SCK
  N6: Raspberry_Pi_B_rev1.GPIO_8, NRF24L1.CSN
  GND: Raspberry_Pi_B_rev1.GND, NRF24L1.GND

custom parts:
  NRF24L01: NRF24L01 module
